# Fritzing sketch backlight (saved by Fritzing 0.9.2b)
breadboards: 1

parts:
  Part1 = Arduino Pro Mini v13
  R1 = Resistor [tolerance=±5% resistance=1k package=THT]
  R2 = Resistor [tolerance=±5% resistance=10k package=THT]
  Q1 = PNP-Transistor [package="TO92 [THT]"]
  J1 = female pin header, 2 pins [form="♀ (female)"]

nets:
  5V: Part1.VCC, R2.Pin_0, Q1.E
  GND: Part1.GND, J1.pin2
  N1: Part1.D9_PWM, R1.Pin_0
  N2: R1.Pin_1, Q1.B
  N3: Q1.C, J1.pin1

notes:
  BL
  Gnd
  LCD pins
