# Fritzing sketch luxmeter (saved by Fritzing 0.9.2b)
breadboards: 1

parts:
  Part1 = Arduino Pro Mini v13
  Nokia_5110_LCD_Module1 = Nokia5110LCDModule
  S1 = Momentary Switch [package=ksa_sealed_tac_switch]
  Part2 = BH1750
  Q1 = PNP-Transistor [package="TO92 [THT]"]
  R1 = Resistor [tolerance=±5% resistance=10k package=THT]
  R2 = Resistor [tolerance=±5% resistance=1k package=THT]
  Power_plug1 = Power plug

nets:
  5V: Part1.VCC, Nokia_5110_LCD_Module1.6_DN_(MOSI), Part2.VCC, Q1.C, Power_plug1.VCC
  N1: Part1.A4, Part2.SDA
  N2: Part1.A5, Part2.SCL
  GND: Part1.GND, S1.4, Part2.GND, R1.Pin_1, Power_plug1.GND
  N3: Part1.D13/SCK, Nokia_5110_LCD_Module1.D/C
  N4: Part1.D11_PWM/MOSI, Nokia_5110_LCD_Module1.RST
  N5: Part1.D9_PWM, R2.Pin_0
  N6: Part1.D5_PWM, Nokia_5110_LCD_Module1.SCE
  N7: Part1.D4, Nokia_5110_LCD_Module1.Grnd
  N8: Part1.D3_PWM, Nokia_5110_LCD_Module1.Vcc
  N9: Part1.D2, S1.2
  N10: Nokia_5110_LCD_Module1.SCLK, Q1.E
  N11: Nokia_5110_LCD_Module1.LED, S1.3
  N12: Q1.B, R1.Pin_0, R2.Pin_1

notes:
  5V in

custom parts:
  : Nokia 5110 LCD with 8 pin. It's a 45mm*45mm module part. Description: The Nokia 5110 is a basic graphic LCD screen for lots of applications. It was originally intended for as a cell phone screen. This one is mounted on an easy to solder PCB. It uses the PCD8544 controller. The PCD8544 is a low power CMOS LCD controller/driver, designed to drive a graphic display of 48 rows and 84 columns. All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
  BH1750: Light Sensor
